# Fritzing sketch MQ-2Breadboard (saved by Fritzing 0.9.1b)
breadboards: 1

parts:
  R1 = Resistor [tolerance=±5% resistance=22k package=THT]
  Arduino1 = Arduino Uno (Rev3)

nets:
  N1: R1.Pin_0, Arduino1.A0
  N2: R1.Pin_1, Arduino1.GND

notes:
  MQ-2 Sensor Pins
  A B
  H H
  A B
  MQ-2 Sensor Wires
  R G
  R W
  R G
  Red wires connected to both A pins and the left H pin and running to the 5V pin on the Arduino
  Green wires connected to both B pins and running to the analog pin A0 on the Arduino
  White wire connected to the right H pin and running to GND on the Arduino.
  A 22K ohms resistor connected to the green wires (analog pin) and the white wire (ground).
  Arduino Uno + MQ-2 (gas & smoke) Sensor
  Derek Erb - 26/02/2013
  http://about.me/derekerb
  derek.erb@gmail.com
